# Fritzing sketch Circut (saved by Fritzing 0.9.3b)
circuit board: 8.46667cm x 5.64444cm
breadboards: 1

parts:
  Pot1 = Rotary Potentiometer (Small) [maximum_resistance=10kΩ package=THT]
  Pot2 = Rotary Potentiometer (Small) [maximum_resistance=10kΩ package=THT]
  Switch = Pushbutton [package="[THT]"]
  Arduino = Arduino Uno (Rev3)

nets:
  N1: Pot1.leg1, Pot2.leg1, Switch.Pin_1, Switch.Pin_2, Arduino.GND
  N2: Pot1.wiper, Arduino.A0
  N3: Pot1.leg2, Pot2.leg2, Arduino.5V
  N4: Pot2.wiper, Arduino.A1
  N5: Switch.Pin_3, Switch.Pin_4, Arduino.D2
